// Logisim project trabalho_final.circ as structural Verilog: 4 circuits, main circuit main
module main (
  input  in_1,
  input  in_2,
  input  in_3,
  input  in_4,
  input  in_5,
  input  in_6,
  input  in_7,
  input  in_8,
  input  [7:0] B,
  input  in_10,
  input  [1:0] Primeiro,
  input  [1:0] Segundo,
  input  [1:0] in_13,
  input  [2:0] in_14,
  output [7:0] out_15
);

  wire clock_1_out, demultiplexer_1_out0, demultiplexer_1_out1, demultiplexer_1_out2, demultiplexer_1_out3;
  wire [7:0] adder_1_out, and_1_out, divider_1_out, multiplexer_1_out, multiplexer_2_out, multiplexer_4_out,
       multiplier_1_out, not_1_out, or_1_out, register_1_q, register_2_q, register_3_q, register_4_q,
       subtractor_1_out, xor_1_out;

  mux_2x1_8bits mux_2x1_8bits_1 (
    .Alsb(in_8), .A1(in_7), .A2(in_6), .A3(in_5), .A4(in_4), .A5(in_3), .A6(in_2), .Amsb(in_1));  // open: blsb, B1, B2, B3, B4, B5, B6, Bmsb, in_17, out_18, out_19, out_20, out_21, out_22, out_23, out_24, out_25
  Clock clock_1 (.out(clock_1_out));
  Adder adder_1 (.a(multiplexer_2_out), .b(multiplexer_4_out), .out(adder_1_out));  // open: cin, cout
  Demultiplexer #(.select(2)) demultiplexer_1 (
    .out0(demultiplexer_1_out0), .out1(demultiplexer_1_out1), .out2(demultiplexer_1_out2),
    .out3(demultiplexer_1_out3), .in(clock_1_out), .sel(in_13));
  Multiplier multiplier_1 (.a(multiplexer_2_out), .b(multiplexer_4_out), .out(multiplier_1_out));  // open: cin, cout
  Multiplexer #(.width(8)) multiplexer_1 (.in0(out_15), .in1(B), .out(multiplexer_1_out), .sel(in_10));
  Register register_1 (.D(multiplexer_1_out), .clk(demultiplexer_1_out0), .Q(register_1_q));  // open: en, clr
  assign xor_1_out = multiplexer_2_out ^ multiplexer_4_out;  // XOR_Gate xor_1, 8 bits wide
  Register register_2 (.D(multiplexer_1_out), .clk(demultiplexer_1_out1), .Q(register_2_q));  // open: en, clr
  Multiplexer #(.select(2), .width(8)) multiplexer_2 (
    .in0(register_1_q), .in1(register_2_q), .in2(register_3_q), .in3(register_4_q), .out(multiplexer_2_out),
    .sel(Primeiro));
  assign and_1_out = multiplexer_2_out & multiplexer_4_out;  // AND_Gate and_1, 8 bits wide
  Multiplexer #(.select(3), .width(8)) multiplexer_3 (
    .in0(multiplier_1_out), .in1(xor_1_out), .in2(adder_1_out), .in3(and_1_out), .in4(or_1_out),
    .in5(not_1_out), .in6(subtractor_1_out), .in7(divider_1_out), .out(out_15), .sel(in_14));
  Register register_3 (.D(multiplexer_1_out), .clk(demultiplexer_1_out2), .Q(register_3_q));  // open: en, clr
  assign or_1_out = multiplexer_2_out | multiplexer_4_out;  // OR_Gate or_1, 8 bits wide
  assign not_1_out = ~multiplexer_4_out;  // NOT_Gate not_1, 8 bits wide
  Register register_4 (.D(multiplexer_1_out), .clk(demultiplexer_1_out3), .Q(register_4_q));  // open: en, clr
  Multiplexer #(.select(2), .width(8)) multiplexer_4 (
    .in0(register_1_q), .in1(register_2_q), .in2(register_3_q), .in3(register_4_q), .out(multiplexer_4_out),
    .sel(Segundo));
  Subtractor subtractor_1 (.a(multiplexer_2_out), .b(multiplexer_4_out), .out(subtractor_1_out));  // open: bin, bout
  Divider divider_1 (.a(multiplexer_2_out), .b(multiplexer_4_out), .out(divider_1_out));  // open: upper, rem
endmodule

module mux_2x1_8bits (
  input  Alsb,
  input  A1,
  input  A2,
  input  A3,
  input  A4,
  input  A5,
  input  A6,
  input  Amsb,
  input  blsb,
  input  B1,
  input  B2,
  input  B3,
  input  B4,
  input  B5,
  input  B6,
  input  Bmsb,
  input  in_17,
  output out_18,
  output out_19,
  output out_20,
  output out_21,
  output out_22,
  output out_23,
  output out_24,
  output out_25
);

  wire and_1_out, and_2_out, and_3_out, and_4_out, and_5_out, and_6_out, and_7_out, and_8_out, and_9_out,
       and_10_out, and_11_out, and_12_out, and_13_out, and_14_out, and_15_out, and_16_out;

  and and_1 (and_1_out, Alsb, ~in_17);  // AND_Gate
  and and_2 (and_2_out, A1, ~in_17);  // AND_Gate
  and and_3 (and_3_out, A2, ~in_17);  // AND_Gate
  and and_4 (and_4_out, A3, ~in_17);  // AND_Gate
  and and_5 (and_5_out, A4, ~in_17);  // AND_Gate
  and and_6 (and_6_out, A5, ~in_17);  // AND_Gate
  and and_7 (and_7_out, A6, ~in_17);  // AND_Gate
  and and_8 (and_8_out, Amsb, ~in_17);  // AND_Gate
  and and_9 (and_9_out, blsb, in_17);
  and and_10 (and_10_out, B1, in_17);
  and and_11 (and_11_out, B2, in_17);
  and and_12 (and_12_out, B3, in_17);
  and and_13 (and_13_out, B4, in_17);
  and and_14 (and_14_out, B5, in_17);
  and and_15 (and_15_out, B6, in_17);
  and and_16 (and_16_out, Bmsb, in_17);
  or or_1 (out_18, and_1_out, and_9_out);
  or or_2 (out_19, and_2_out, and_10_out);
  or or_3 (out_20, and_3_out, and_11_out);
  or or_4 (out_21, and_4_out, and_12_out);
  or or_5 (out_22, and_5_out, and_13_out);
  or or_6 (out_23, and_6_out, and_14_out);
  or or_7 (out_24, and_7_out, and_15_out);
  or or_8 (out_25, and_8_out, and_16_out);
endmodule

module mux_4x2_1bit (
  input  Alsb,
  input  A1,
  input  A2,
  input  Amsb,
  input  msb,
  input  lsb,
  output out_7
);

  wire and_1_out, and_2_out, and_3_out, and_4_out;

  and and_1 (and_1_out, Alsb, ~msb, ~lsb);  // AND_Gate
  and and_2 (and_2_out, A1, lsb, ~msb);  // AND_Gate
  and and_3 (and_3_out, A2, ~lsb, msb);  // AND_Gate
  and and_4 (and_4_out, Amsb, lsb, msb);
  or or_1 (out_7, and_1_out, and_2_out, and_3_out, and_4_out);
endmodule

module registrador_8bits (
  input  in_1
);

  wire clock_1_out, nand_1_out, nand_2_out, nand_3_out, nand_4_out, not_1_out;

  not not_1 (not_1_out, in_1);
  Clock clock_1 (.out(clock_1_out));
  nand nand_1 (nand_1_out, in_1, clock_1_out);
  nand nand_2 (nand_2_out, not_1_out, clock_1_out);
  nand nand_3 (nand_3_out, nand_1_out, nand_4_out);
  nand nand_4 (nand_4_out, nand_3_out, nand_2_out);
endmodule
