// Logisim project Atividade_1.circ as structural Verilog: 1 circuit, main circuit main
module main (
  input  in_1,
  input  in_2,
  input  in_3,
  output out_4
);

  wire nand_1_out, nor_1_out, xor_1_out;

  nor nor_1 (nor_1_out, in_1, ~in_2, in_3);  // NOR_Gate
  nand nand_1 (nand_1_out, nor_1_out, ~in_2);  // NAND_Gate
  xor xor_1 (xor_1_out, nor_1_out, nand_1_out);
  not not_1 (out_4, xor_1_out);
endmodule
