// Logisim project bcd_to_7seg.circ as structural Verilog: 1 circuit, main circuit main
module main (
  input  A,
  input  B,
  input  C,
  input  D
);

  wire and_1_out, and_2_out, and_3_out, and_4_out, and_5_out, and_6_out, and_7_out, and_8_out, and_9_out,
       and_10_out, and_11_out, and_12_out, and_13_out, and_14_out, and_15_out, and_16_out, or_1_out,
       or_2_out, or_3_out, or_4_out, or_5_out, or_6_out, or_7_out;

  and and_1 (and_1_out, ~B, ~D);  // AND_Gate
  and and_2 (and_2_out, ~B, ~D);  // AND_Gate
  and and_3 (and_3_out, ~D, C);  // AND_Gate
  and and_4 (and_4_out, ~B, C);  // AND_Gate
  and and_5 (and_5_out, ~C, B, D);  // AND_Gate
  and and_6 (and_6_out, ~B, ~D);  // AND_Gate
  and and_7 (and_7_out, ~D, ~C);  // AND_Gate
  and and_8 (and_8_out, ~D, B);  // AND_Gate
  and and_9 (and_9_out, ~C, B);  // AND_Gate
  and and_10 (and_10_out, ~C, B);  // AND_Gate
  and and_11 (and_11_out, ~D, C);  // AND_Gate
  and and_12 (and_12_out, ~B, C);  // AND_Gate
  and and_13 (and_13_out, D, B);
  and and_14 (and_14_out, ~C, ~D);  // AND_Gate
  and and_15 (and_15_out, C, D);
  and and_16 (and_16_out, ~D, C);  // AND_Gate
  or or_1 (or_1_out, A, C, and_1_out, and_13_out);
  or or_2 (or_2_out, and_6_out, and_16_out);
  or or_3 (or_3_out, A, and_7_out, and_8_out, and_9_out);
  or or_4 (or_4_out, A, and_10_out, and_11_out, and_12_out);
  or or_5 (or_5_out, ~B, and_14_out, and_15_out);  // OR_Gate
  or or_6 (or_6_out, ~C, D, B);  // OR_Gate
  or or_7 (or_7_out, A, and_2_out, and_3_out, and_4_out, and_5_out);
  _7_Segment_Display u_7_segment_display_1 (
    .g(or_4_out), .f(or_3_out), .a(or_1_out), .b(or_5_out), .e(or_2_out), .d(or_7_out), .c(or_6_out));  // open: dp
endmodule
