// Logisim project bcd_to_decimal.circ as structural Verilog: 1 circuit, main circuit main
module main (
  input  A,
  input  B,
  input  C,
  input  D,
  output out_5
);

  wire Cinco_out, Dois_out, Nove_out, Oito_out, Quatro_out, Seis_out, Sete_out, Tres_out, Um_out, Zero_out;

  and Zero (Zero_out, ~D, ~C, ~B, ~A);  // AND_Gate
  and Um (Um_out, D, ~C, ~B, ~A);  // AND_Gate
  and Dois (Dois_out, ~D, C, ~B, ~A);  // AND_Gate
  and Tres (Tres_out, D, C, ~B, ~A);  // AND_Gate
  and Quatro (Quatro_out, ~D, ~C, B, ~A);  // AND_Gate
  and Cinco (Cinco_out, D, ~C, B, ~A);  // AND_Gate
  and Seis (Seis_out, ~D, C, B, ~A);  // AND_Gate
  and Sete (Sete_out, D, C, B, ~A);  // AND_Gate
  and Oito (Oito_out, ~D, ~C, ~B, A);  // AND_Gate
  and Nove (Nove_out, D, ~C, ~B, A);  // AND_Gate
  or or_1 (out_5, Zero_out, Um_out, Dois_out, Tres_out, Quatro_out, Cinco_out, Seis_out, Sete_out, Oito_out, Nove_out);
endmodule
