// Logisim project decimal_to_bcd_v1.circ as structural Verilog
module teste (
  input  Nove,
  input  Oito,
  input  Sete,
  input  Seis,
  input  Cinco,
  input  Quatro,
  input  Tres,
  input  Dois,
  input  Um,
  input  Zero,
  output A,
  output B,
  output C,
  output D
);

  or or_1 (A, Oito, Nove);
  or or_2 (B, Quatro, Cinco, Seis, Sete);
  or or_3 (C, Dois, Tres, Seis, Sete);
  or or_4 (D, Um, Tres, Cinco, Sete, Nove);
endmodule
