// Logisim project demux_1x2.circ as structural Verilog: 1 circuit, main circuit main
module main (
  input  E,
  input  A,
  output S0,
  output S1
);

  and and_1 (S0, E, ~A);  // AND_Gate
  and and_2 (S1, E, A);
endmodule
