// Logisim project demux_1x4.circ as structural Verilog: 1 circuit, main circuit main
module main (
  input  E,
  input  A,
  input  B,
  output S0,
  output S1,
  output S2,
  output S3
);

  and and_1 (S0, E, ~B, ~A);  // AND_Gate
  and and_2 (S1, E, B, ~A);  // AND_Gate
  and and_3 (S2, E, ~B, A);  // AND_Gate
  and and_4 (S3, E, B, A);
endmodule
