// Logisim project demux_1x4_3BITS.circ as structural Verilog: 1 circuit, main circuit main
module main (
  input  MSB,
  input  I2,
  input  LSB,
  input  in_4,
  input  in_5,
  output S11,
  output S21,
  output S31,
  output S41,
  output S12,
  output S22,
  output S32,
  output S42,
  output S13,
  output S23,
  output S33,
  output S43
);

  and and_1 (S11, MSB, ~in_5, ~in_4);  // AND_Gate
  and and_2 (S21, MSB, in_5, ~in_4);  // AND_Gate
  and and_3 (S31, MSB, ~in_5, in_4);  // AND_Gate
  and and_4 (S41, MSB, in_5, in_4);
  and and_5 (S12, I2, ~in_5, ~in_4);  // AND_Gate
  and and_6 (S22, I2, in_5, ~in_4);  // AND_Gate
  and and_7 (S32, I2, ~in_5, in_4);  // AND_Gate
  and and_8 (S42, I2, in_5, in_4);
  and and_9 (S13, LSB, ~in_5, ~in_4);  // AND_Gate
  and and_10 (S23, LSB, in_5, ~in_4);  // AND_Gate
  and and_11 (S33, LSB, ~in_5, in_4);  // AND_Gate
  and and_12 (S43, LSB, in_5, in_4);
endmodule
