// Logisim project mux_3bit_assossiado.circ as structural Verilog: 1 circuit, main circuit main
module main (
  input  in_1,
  input  in_2,
  input  in_3,
  input  in_4,
  input  in_5,
  input  in_6,
  input  in_7,
  input  in_8,
  input  in_9,
  input  in_10,
  input  in_11,
  output out_12,
  output out_13,
  output out_14
);

  wire and_1_out, and_2_out, and_3_out, and_4_out, and_5_out, and_6_out, and_7_out, and_8_out, and_9_out;

  and and_1 (and_1_out, in_1, ~in_11, ~in_10);  // AND_Gate
  and and_2 (and_2_out, in_2, ~in_11, in_10);  // AND_Gate
  and and_3 (and_3_out, in_3, in_11, ~in_10);  // AND_Gate
  and and_4 (and_4_out, in_4, ~in_11, ~in_10);  // AND_Gate
  and and_5 (and_5_out, in_5, ~in_11, in_10);  // AND_Gate
  and and_6 (and_6_out, in_6, in_11, ~in_10);  // AND_Gate
  and and_7 (and_7_out, in_7, ~in_11, ~in_10);  // AND_Gate
  and and_8 (and_8_out, in_8, ~in_11, in_10);  // AND_Gate
  and and_9 (and_9_out, in_9, in_11, ~in_10);  // AND_Gate
  or or_1 (out_12, and_1_out, and_2_out, and_3_out);
  or or_2 (out_13, and_4_out, and_5_out, and_6_out);
  or or_3 (out_14, and_7_out, and_8_out, and_9_out);
endmodule
