// Logisim project mux_4x1.circ as structural Verilog: 1 circuit, main circuit main
module main (
  input  A,
  input  B,
  input  C,
  input  D,
  input  Sel1,
  input  Sel0,
  output out_7
);

  wire and_1_out, and_2_out, and_3_out, and_4_out;

  and and_1 (and_1_out, ~Sel1, ~Sel0, A);  // AND_Gate
  and and_2 (and_2_out, ~Sel1, Sel0, B);  // AND_Gate
  and and_3 (and_3_out, Sel1, ~Sel0, C);  // AND_Gate
  and and_4 (and_4_out, Sel1, Sel0, D);
  or or_1 (out_7, and_1_out, and_2_out, and_3_out, and_4_out);
endmodule
