// Logisim project mux_demux.circ as structural Verilog: 1 circuit, main circuit main
module main (
  input  A,
  input  B,
  input  C,
  input  D,
  input  Sel1,
  input  Sel0,
  input  Sel3,
  input  Sel2,
  output F1,
  output F2,
  output F3,
  output F4
);

  wire and_1_out, and_2_out, and_3_out, and_4_out, or_1_out;

  and and_1 (and_1_out, A, ~Sel0, ~Sel1);  // AND_Gate
  and and_2 (and_2_out, B, Sel0, ~Sel1);  // AND_Gate
  and and_3 (and_3_out, C, ~Sel0, Sel1);  // AND_Gate
  and and_4 (and_4_out, D, Sel0, Sel1);
  or or_1 (or_1_out, and_1_out, and_2_out, and_3_out, and_4_out);
  and and_5 (F1, or_1_out, ~Sel2, ~Sel3);  // AND_Gate
  and and_6 (F2, or_1_out, Sel2, ~Sel3);  // AND_Gate
  and and_7 (F3, or_1_out, ~Sel2, Sel3);  // AND_Gate
  and and_8 (F4, or_1_out, Sel2, Sel3);
endmodule
