// Logisim project trabalho_final.circ as structural Verilog: 1 circuit, main circuit main
module main (
  input  [7:0] B,
  input  in_2,
  input  [1:0] Primeiro,
  input  [1:0] Segundo,
  input  [1:0] in_5,
  input  [2:0] in_6,
  output [7:0] out_7
);

  wire clock_1_out, demultiplexer_1_out0, demultiplexer_1_out1, demultiplexer_1_out2, demultiplexer_1_out3;
  wire [7:0] adder_1_out, and_1_out, divider_1_out, multiplexer_1_out, multiplexer_2_out, multiplexer_4_out,
       multiplier_1_out, not_1_out, or_1_out, register_1_q, register_2_q, register_3_q, register_4_q,
       subtractor_1_out, xor_1_out;

  Clock clock_1 (.out(clock_1_out));
  Demultiplexer #(.select(2)) demultiplexer_1 (
    .out0(demultiplexer_1_out0), .out1(demultiplexer_1_out1), .out2(demultiplexer_1_out2),
    .out3(demultiplexer_1_out3), .in(clock_1_out), .sel(in_5));
  Adder adder_1 (.a(multiplexer_2_out), .b(multiplexer_4_out), .out(adder_1_out));  // open: cin, cout
  Multiplexer #(.width(8)) multiplexer_1 (.in0(out_7), .in1(B), .out(multiplexer_1_out), .sel(in_2));
  Register register_1 (.D(multiplexer_1_out), .clk(demultiplexer_1_out0), .Q(register_1_q));  // open: en, clr
  Multiplier multiplier_1 (.a(multiplexer_2_out), .b(multiplexer_4_out), .out(multiplier_1_out));  // open: cin, cout
  assign xor_1_out = multiplexer_2_out ^ multiplexer_4_out;  // XOR_Gate xor_1, 8 bits wide
  Register register_2 (.D(multiplexer_1_out), .clk(demultiplexer_1_out1), .Q(register_2_q));  // open: en, clr
  Multiplexer #(.select(2), .width(8)) multiplexer_2 (
    .in0(register_1_q), .in1(register_2_q), .in2(register_3_q), .in3(register_4_q), .out(multiplexer_2_out),
    .sel(Primeiro));
  assign and_1_out = multiplexer_2_out & multiplexer_4_out;  // AND_Gate and_1, 8 bits wide
  Multiplexer #(.select(3), .width(8)) multiplexer_3 (
    .in0(multiplier_1_out), .in1(xor_1_out), .in2(adder_1_out), .in3(and_1_out), .in4(or_1_out),
    .in5(not_1_out), .in6(subtractor_1_out), .in7(divider_1_out), .out(out_7), .sel(in_6));
  Register register_3 (.D(multiplexer_1_out), .clk(demultiplexer_1_out2), .Q(register_3_q));  // open: en, clr
  assign or_1_out = multiplexer_2_out | multiplexer_4_out;  // OR_Gate or_1, 8 bits wide
  assign not_1_out = ~multiplexer_4_out;  // NOT_Gate not_1, 8 bits wide
  Register register_4 (.D(multiplexer_1_out), .clk(demultiplexer_1_out3), .Q(register_4_q));  // open: en, clr
  Multiplexer #(.select(2), .width(8)) multiplexer_4 (
    .in0(register_1_q), .in1(register_2_q), .in2(register_3_q), .in3(register_4_q), .out(multiplexer_4_out),
    .sel(Segundo));
  Subtractor subtractor_1 (.a(multiplexer_2_out), .b(multiplexer_4_out), .out(subtractor_1_out));  // open: bin, bout
  Divider divider_1 (.a(multiplexer_2_out), .b(multiplexer_4_out), .out(divider_1_out));  // open: upper, rem
endmodule
