// Digital circuit contador_assincrono.dig as structural Verilog
module contador_assincrono (
  input  clk,
  output out_2,
  output out_3,
  output out_4,
  output out_5
);

  JK_FF jk_ff_1 (.J(1'b1), .C(~out_4), .K(1'b1), .Q(out_5));  // open: nQ
  JK_FF jk_ff_2 (.J(1'b1), .C(~out_3), .K(1'b1), .Q(out_4));  // open: nQ
  JK_FF jk_ff_3 (.J(1'b1), .C(~out_2), .K(1'b1), .Q(out_3));  // open: nQ
  JK_FF jk_ff_4 (.J(1'b1), .C(~clk), .K(1'b1), .Q(out_2));  // open: nQ
endmodule
