// Digital circuit basico.dig as structural Verilog
module basico (
  input  in_1,
  input  in_2,
  input  in_4,
  input  in_5,
  input  in_7,
  input  in_8,
  output out_3,
  output out_6,
  output out_9
);

  algoritmica #(.applicationType("GHDL")) u_algoritmica (.A(in_1), .B(in_2), .S(out_3));
  hw #(.applicationType("GHDL")) u_hw (.A(in_4), .B(in_5), .S(out_6));
  fluxo #(.applicationType("GHDL")) u_fluxo (.A(in_7), .B(in_8), .S(out_9));
endmodule

/* Code of algoritmica:
library ieee;
use ieee.std_logic_1164.all;

entity algoritmica is
	port(
		A: in STD_LOGIC;
		B: in STD_LOGIC;
		S: out STD_LOGIC
	);
end algoritmica;

architecture comport_algor of algoritmica is
begin
	process(A,B)
	begin
		if(B < A) then
			S <= '1';
		else
			s <= '0';
		end if;
	end process;
end comport_algor;
*/

/* Code of hw:
library ieee;
use ieee.std_logic_1164.all;

entity hw is
        port(
            A: in STD_LOGIC;
            B: in STD_LOGIC;
            S: out STD_LOGIC
        );
end hw;

architecture comportamento of hw is
begin

	s <= A and B;

end comportamento;
*/

/* Code of fluxo:
library ieee;
use ieee.STD_LOGIC_1164.all;

entity fluxo is
	port (
		A: in STD_LOGIC;
		B: in STD_LOGIC;
		S: out STD_LOGIC
	);
end fluxo;

architecture comport_fluxo of fluxo is
begin
	s <= '1' when B < A
		else '0';
end comport_fluxo;
*/
