// Digital circuit circuito.dig as structural Verilog
module circuito (
  input  A,
  input  B,
  output SUM,
  output CARRY
);

  half_adder #(.applicationType("GHDL")) u_half_adder (.A(A), .B(B), .SUM(SUM), .CARRY(CARRY));
  full_adder #(.applicationType("GHDL")) u_full_adder ();  // open: a_f, b_f, carry_in, carry_out, sum
endmodule

/* Test case Teste para o half_adder:
A B SUM CARRY
0 0 0 0
1 0 1 0
0 1 1 0
1 1 0 1
*/

/* Code of half_adder:
library ieee;
use ieee.STD_LOGIC_1164.all;

entity half_adder is
	port (
		A: in STD_LOGIC;
		B: in STD_LOGIC;
		SUM: out STD_LOGIC;
		CARRY: out STD_LOGIC
	);
end half_adder;


architecture behavior_algoritmica of half_adder is
begin
	process(A, B)
	begin
		if(A = '1' and B = '1') then
			SUM <= '0';
			CARRY <= '1';
		elsif ( A > B or B > A ) then
			SUM <= '1';
			CARRY <= '0';
		else
			SUM <= '0';
			CARRY <= '0';
		end if;
	end process;

end behavior_algoritmica;


--------------------------
-- Abstração de fluxo
--------------------------
-- architecture behavior_fluxo of half_adder is
-- begin

--	SUM <= A xor B;
--	CARRY <= A and B;

-- end behavior_fluxo;
*/

/* Code of full_adder:
LIBRARY ieee;
USE ieee.std_logic_1164.ALL;

ENTITY full_adder IS
    PORT (
       a_f,b_f: in STD_LOGIC;
       carry_in: in STD_LOGIC;
       carry_out, sum: out STD_LOGIC
    );
END ENTITY full_adder;

ARCHITECTURE behav_estrutural OF full_adder IS
    component half_adder IS
    PORT (
        a,b: in STD_LOGIC;
        carry, sum: out STD_LOGIC
    );
    END component;

    signal carry1, carry2, sum_int: STD_LOGIC;

BEGIN
   
    ha1: half_adder
     port map(
        a => a_f,
        b => b_f,
        carry => carry1,
        sum => sum_int
    );

    ha2: half_adder
    port map(
       a => sum_int,
       b => carry_in,
       carry => carry2,
       sum => sum
   );

   carry_out <= carry1 OR carry2;

END behav_estrutural;

----------------------------------------
--ENTITY half_adder
-----------------------------------------
LIBRARY ieee;
USE ieee.std_logic_1164.ALL;

ENTITY half_adder IS
    PORT (
       a,b: in STD_LOGIC;
       carry, sum: out STD_LOGIC
    );
END ENTITY half_adder;

ARCHITECTURE behav_FLUXO OF half_adder IS
BEGIN
   carry <= a AND b;
   sum <= a XOR b;
END behav_FLUXO;



-- ARCHITECTURE behav_algo OF half_adder IS
-- BEGIN
--     process (a,b)
--     begin
--         if ( a = '1' and b = '1') then 
--             sum <= '0';
--             carry <= '1';
--         elsif (a > b or b > a) then
--             sum <= '1'; 
--             carry <= '0';
--         else
--             sum <= '0'; 
--             carry <= '0';
--         end if;
--     end process; 
-- END behav_algo;
*/
