// Digital circuit exer_2.dig as structural Verilog
module exer_2 (
  input  [1:0] A,
  input  EN,
  output [3:0] Y_L
);

  decoder_2to4en #(.applicationType("GHDL")) u_decoder_2to4en (.EN(EN), .A(A), .Y_L(Y_L));
endmodule

/* Test case Teste Exercicio 2:
A EN Y_L
0 0 0xf
1 0 0xf
2 0 0xf
3 0 0xf
0 1 1
1 1 2
2 1 4
3 1 8
*/

/* Code of decoder_2to4en:
library ieee;
use ieee.std_logic_1164.all;

entity decoder_2to4en is
	port (
		EN : in std_logic; -- Enable
		A : in std_logic_vector (1 downto 0); -- Decoder Input
		Y_L : out std_logic_vector (3 downto 0) -- Decoder Output (active low)
	);
end entity decoder_2to4en;

architecture behavior of decoder_2to4en is
begin
	process(EN, A)
	begin	
		if EN = '0' then
			Y_L <= "1111";
		else
			case A is
				when "00" => Y_L <= "0001";
				when "01" => Y_L <= "0010";
				when "10" => Y_L <= "0100";
				when "11" => Y_L <= "1000";
				when others => NULL;
			end case;
		end if;
	end process;
end behavior;
*/
