// Digital circuit exercicios_sintaxe.dig as structural Verilog
module exercicios_sintaxe (
  input  in_1,
  input  in_2,
  input  in_3,
  input  in_4,
  input  [3:0] in_6,
  input  in_8,
  input  in_9,
  input  in_10,
  output out_5,
  output out_7,
  output out_11,
  output out_12,
  output out_13
);

  port_or #(.applicationType("GHDL")) u_port_or (.A(in_1), .B(in_2), .C(in_3), .D(in_4), .S(out_5));
  array_or #(.applicationType("GHDL")) u_array_or (.E(in_6), .S(out_7));
  ext3a #(.applicationType("GHDL")) u_ext3a (.A(in_8), .B(in_9), .C(in_10), .D(out_11), .E(out_13), .F(out_12));
endmodule

/* Code of port_or:
library ieee;
use ieee.STD_LOGIC_1164.all;

entity port_or is
	port (
		A: in STD_LOGIC;
		B: in STD_LOGIC;
		C: in STD_LOGIC;
		D: in STD_LOGIC;
		S: out STD_LOGIC
	);
end port_or;

architecture behavior of port_or is
begin

	S <= A or B or C or D;
	
end behavior;
*/

/* Code of array_or:
library ieee;
use ieee.STD_LOGIC_1164.all;

entity array_or is
	port (
		E: in STD_LOGIC_VECTOR (3 DOWNTO 0);
		S: out STD_LOGIC
	);
end array_or;

architecture behavior of array_or is
begin

	S <= E(0) or E(1) or E(2) or E(3);

end behavior;
*/

/* Code of ext3a:
library ieee;
use ieee.STD_LOGIC_1164.all;

entity ext3a is
	port (
		A: in STD_LOGIC;
		B: in STD_LOGIC;
		C: in STD_LOGIC;
		
		D: out STD_LOGIC;
		E: out STD_LOGIC;
		F: out STD_LOGIC
	);
end ext3a;

architecture behavioral of ext3a is
signal nor_AnB, nand_nBnC, and_nBnC:  STD_LOGIC;
begin
	
	nor_AnB <= A nor not B;
	nand_nBnC <= not B nand not C;
	and_nBnC <= not B and not C;
	
	D <= nor_Anb xor not nand_nBnC;
	E <= nand_nBnC and not B;
	F <= nand_nBnC xor and_nBnC;

end behavioral;
*/
