// Digital circuit Contador_Gray.dig as structural Verilog
module Contador_Gray (
  input  clk
);

  wire and_1_out, and_2_out, and_3_out, and_4_out, and_5_out, and_6_out, and_7_out, and_8_out, and_9_out,
       and_10_out, and_11_out, and_12_out, and_13_out, and_14_out, and_15_out, and_16_out, or_1_out,
       or_2_out, or_3_out, or_4_out, Q0_nq, Q0_q, Q1_nq, Q1_q, Q2_nq, Q2_q, Q3_nq, Q3_q;

  and and_1 (and_1_out, Q3_nq, Q2_nq, Q1_q);
  and and_2 (and_2_out, Q3_nq, Q2_q, Q1_nq);
  and and_3 (and_3_out, Q3_q, Q2_q, Q1_q);
  and and_4 (and_4_out, Q2_nq, Q1_nq, Q3_q);
  or or_1 (or_1_out, and_1_out, and_2_out, and_3_out, and_4_out);
  and and_5 (and_5_out, Q3_nq, Q2_nq, Q1_nq);
  and and_6 (and_6_out, Q3_q, Q2_q, Q1_nq);
  and and_7 (and_7_out, Q3_nq, Q2_q, Q1_q);
  and and_8 (and_8_out, Q3_q, Q2_nq, Q1_q);
  or or_2 (or_2_out, and_5_out, and_6_out, and_7_out, and_8_out);
  and and_9 (and_9_out, Q3_nq, Q2_q, Q0_q);
  and and_10 (and_10_out, Q0_q, Q3_q, Q2_nq);
  or or_3 (or_3_out, and_9_out, and_10_out);
  and and_11 (and_11_out, Q3_nq, Q2_nq, Q0_q);
  and and_12 (and_12_out, Q0_q, Q3_q, Q2_q);
  or or_4 (or_4_out, and_11_out, and_12_out);
  and and_13 (and_13_out, Q3_nq, Q1_q, Q0_nq);
  and and_14 (and_14_out, Q1_q, Q0_nq, Q3_q);
  and and_15 (and_15_out, Q2_q, Q1_nq, Q0_nq);
  and and_16 (and_16_out, Q1_nq, Q0_nq, Q2_nq);
  JK_FF Q3 (.J(and_15_out), .C(~clk), .K(and_16_out), .Q(Q3_q), .nQ(Q3_nq));
  JK_FF Q2 (.J(and_13_out), .C(~clk), .K(and_14_out), .Q(Q2_q), .nQ(Q2_nq));
  LED led_1 (.in(Q3_q));
  LED led_2 (.in(Q2_q));
  LED led_3 (.in(Q1_q));
  LED led_4 (.in(Q0_q));
  JK_FF Q1 (.J(or_4_out), .C(~clk), .K(or_3_out), .Q(Q1_q), .nQ(Q1_nq));
  JK_FF Q0 (.J(or_2_out), .C(~clk), .K(or_1_out), .Q(Q0_q), .nQ(Q0_nq));
endmodule
