// Digital circuit Implementacao_debug.dig as structural Verilog
module Implementacao_debug (
  input  clk,
  input  rst,
  input  start,
  input  hit,
  input  stay,
  input  random,
  input  [3:0] cards
);

  wire u_blackjack_carta_1_dealer, u_blackjack_carta_2_dealer, u_blackjack_carta_user_1,
       u_blackjack_carta_user_2, u_blackjack_comparar_cartas, u_blackjack_esperar_dealer,
       u_blackjack_esperar_user, u_blackjack_hit, u_blackjack_inicio, u_blackjack_lose_out,
       u_blackjack_nova_carta_dealer, u_blackjack_stay, u_blackjack_tie, u_blackjack_tie_out,
       u_blackjack_user_ganhou, u_blackjack_user_perdeu, u_blackjack_win_out;
  wire [3:0] u_blackjack_card_display;
  wire [6:0] not_1_out, not_2_out, not_3_out, u_BCD_to_7Segment_card_display,
       u_Display_Controller_sum_d_display, u_Display_Controller_sum_u_display;
  wire [7:0] u_blackjack_sum_display;

  Display_Controller #(.applicationType("GHDL")) u_Display_Controller (
    .sum_display(u_blackjack_sum_display), .sum_u_display(u_Display_Controller_sum_u_display),
    .sum_d_display(u_Display_Controller_sum_d_display));
  blackjack #(.applicationType("GHDL")) u_blackjack (
    .clk(clk), .rst(rst), .start(start), .hit_btn(hit), .stay_btn(stay), .random_cards(random),
    .cards(cards), .win_out(u_blackjack_win_out), .lose_out(u_blackjack_lose_out),
    .tie_out(u_blackjack_tie_out), .card_display(u_blackjack_card_display),
    .sum_display(u_blackjack_sum_display), .INICIO(u_blackjack_inicio),
    .CARTA_USER_1(u_blackjack_carta_user_1), .CARTA_USER_2(u_blackjack_carta_user_2),
    .ESPERAR_USER(u_blackjack_esperar_user), .HIT(u_blackjack_hit), .STAY(u_blackjack_stay),
    .CARTA_1_DEALER(u_blackjack_carta_1_dealer), .CARTA_2_DEALER(u_blackjack_carta_2_dealer),
    .NOVA_CARTA_DEALER(u_blackjack_nova_carta_dealer), .ESPERAR_DEALER(u_blackjack_esperar_dealer),
    .COMPARAR_CARTAS(u_blackjack_comparar_cartas), .USER_GANHOU(u_blackjack_user_ganhou),
    .USER_PERDEU(u_blackjack_user_perdeu), .TIE(u_blackjack_tie));
  assign not_1_out = ~u_Display_Controller_sum_d_display;  // Not not_1, 7 bits wide
  BCD_to_7Segment #(.applicationType("GHDL")) u_BCD_to_7Segment (
    .BCD(u_blackjack_card_display), .card_display(u_BCD_to_7Segment_card_display));
  Seven_Seg seven_seg_1 (
    .a(not_1_out[0]), .b(not_1_out[1]), .c(not_1_out[2]), .d(not_1_out[3]), .e(not_1_out[4]),
    .f(not_1_out[5]), .g(not_1_out[6]), .dp(1'b1));
  assign not_2_out = ~u_Display_Controller_sum_u_display;  // Not not_2, 7 bits wide
  LED WIN_OUT (.in(u_blackjack_win_out));
  LED LOSE_OUT (.in(u_blackjack_lose_out));
  LED TIE_OUT (.in(u_blackjack_tie_out));
  assign not_3_out = ~u_BCD_to_7Segment_card_display;  // Not not_3, 7 bits wide
  Seven_Seg seven_seg_2 (
    .a(not_2_out[0]), .b(not_2_out[1]), .c(not_2_out[2]), .d(not_2_out[3]), .e(not_2_out[4]),
    .f(not_2_out[5]), .g(not_2_out[6]), .dp(1'b1));
  LED INICIO (.in(u_blackjack_inicio));
  LED CARTA_USER_1 (.in(u_blackjack_carta_user_1));
  LED CARTA_USER_2 (.in(u_blackjack_carta_user_2));
  LED ESPERAR_USER (.in(u_blackjack_esperar_user));
  LED u_HIT (.in(u_blackjack_hit));
  LED u_STAY (.in(u_blackjack_stay));
  LED CARTA_1_DEALER (.in(u_blackjack_carta_1_dealer));
  LED CARTA_2_DEALER (.in(u_blackjack_carta_2_dealer));
  LED NOVA_CARTA_DEALER (.in(u_blackjack_nova_carta_dealer));
  LED ESPERAR_DEALER (.in(u_blackjack_esperar_dealer));
  LED COMPARAR_CARTAS (.in(u_blackjack_comparar_cartas));
  LED USER_GANHOU (.in(u_blackjack_user_ganhou));
  LED USER_PERDEU (.in(u_blackjack_user_perdeu));
  LED TIE (.in(u_blackjack_tie));
  Seven_Seg seven_seg_3 (
    .a(not_3_out[0]), .b(not_3_out[1]), .c(not_3_out[2]), .d(not_3_out[3]), .e(not_3_out[4]),
    .f(not_3_out[5]), .g(not_3_out[6]), .dp(1'b1));
endmodule

/* Code of Display_Controller:
library IEEE;
use IEEE.STD_LOGIC_1164.ALL;
use IEEE.NUMERIC_STD.ALL;

entity Display_Controller is
    Port (
        sum_display : in STD_LOGIC_VECTOR(7 downto 0);
        -- Saídas para o primeiro display (unidades)
        sum_u_display: out STD_LOGIC_VECTOR(6 downto 0);
        sum_d_display: out STD_LOGIC_VECTOR(6 downto 0)
    );
end Display_Controller;

architecture Behavioral of Display_Controller is
    -- Sinais intermediários para armazenar valores decimais
    signal binary_value : integer range 0 to 255;
    signal tens, ones : integer range 0 to 9;
    signal tens_bcd, ones_bcd : STD_LOGIC_VECTOR(3 downto 0);

begin
    -- Converte o valor binário para inteiro
    binary_value <= to_integer(unsigned(sum_display));
    
    -- Calcula dezenas e unidades
    tens <= binary_value / 10;
    ones <= binary_value mod 10;
    
    -- Converte os valores para BCD
    tens_bcd <= std_logic_vector(to_unsigned(tens, 4));
    ones_bcd <= std_logic_vector(to_unsigned(ones, 4));
    
    -- Processo para decodificar o dígito das unidades
    process(ones_bcd)
    begin
        case ones_bcd is
            when "0000" => -- 0
                sum_u_display <= "1000000";  -- 7-segment display para 0
            when "0001" => -- 1
                sum_u_display <= "1111001";  -- 7-segment display para 1
            when "0010" => -- 2
                sum_u_display <= "0100100";  -- 7-segment display para 2
            when "0011" => -- 3
                sum_u_display <= "0110000";  -- 7-segment display para 3
            when "0100" => -- 4
                sum_u_display <= "0011001";  -- 7-segment display para 4
            when "0101" => -- 5
                sum_u_display <= "0010010";  -- 7-segment display para 5
            when "0110" => -- 6
                sum_u_display <= "0000010";  -- 7-segment display para 6
            when "0111" => -- 7
                sum_u_display <= "1111000";  -- 7-segment display para 7
            when "1000" => -- 8
                sum_u_display <= "0000000";  -- 7-segment display para 8
            when "1001" => -- 9
                sum_u_display <= "0010000";  -- 7-segment display para 9
            when others => 
                sum_u_display <= "0000000";  -- Desativa todos os segmentos
        end case;
    end process;
    
    -- Processo para decodificar o dígito das dezenas
    process(tens_bcd)
    begin
        case tens_bcd is
            when "0000" => -- 0
                sum_d_display <= "1000000";  -- 7-segment display para 0
            when "0001" => -- 1
                sum_d_display <= "1111001";  -- 7-segment display para 1
            when "0010" => -- 2
                sum_d_display <= "0100100";  -- 7-segment display para 2
            when "0011" => -- 3
                sum_d_display <= "0110000";  -- 7-segment display para 3
            when "0100" => -- 4
                sum_d_display <= "0011001";  -- 7-segment display para 4
            when "0101" => -- 5
                sum_d_display <= "0010010";  -- 7-segment display para 5
            when "0110" => -- 6
                sum_d_display <= "0000010";  -- 7-segment display para 6
            when "0111" => -- 7
                sum_d_display <= "1111000";  -- 7-segment display para 7
            when "1000" => -- 8
                sum_d_display <= "0000000";  -- 7-segment display para 8
            when "1001" => -- 9
                sum_d_display <= "0010000";  -- 7-segment display para 9
            when others => 
                sum_d_display <= "0000000";  -- Desativa todos os segmentos
        end case;
    end process;


    
end Behavioral;
*/

/* Code of blackjack:
library IEEE;
use IEEE.STD_LOGIC_1164.ALL;
use IEEE.NUMERIC_STD.ALL;

entity blackjack is
    Port ( 
        clk         : in  STD_LOGIC;
        rst         : in  STD_LOGIC;
        start       : in  STD_LOGIC;
        hit_btn     : in  STD_LOGIC;
        stay_btn    : in  STD_LOGIC;
        random_cards: in  STD_LOGIC;  
        cards       : in  STD_LOGIC_VECTOR(3 downto 0);
        
        win_out     : out STD_LOGIC;
        lose_out    : out STD_LOGIC;
        tie_out     : out STD_LOGIC;
        card_display: out STD_LOGIC_VECTOR(3 downto 0);
        sum_display : out STD_LOGIC_VECTOR(7 downto 0);



            -- debug do estado atual
            INICIO : out STD_LOGIC;
            CARTA_USER_1 : out STD_LOGIC;
            CARTA_USER_2 : out STD_LOGIC;
            ESPERAR_USER: out STD_LOGIC;
            HIT : out STD_LOGIC;
            STAY : out STD_LOGIC;
            CARTA_1_DEALER : out STD_LOGIC;
            CARTA_2_DEALER : out STD_LOGIC;
            NOVA_CARTA_DEALER : out STD_LOGIC;
            ESPERAR_DEALER : out STD_LOGIC;
            COMPARAR_CARTAS : out STD_LOGIC;
            USER_GANHOU : out STD_LOGIC;
            USER_PERDEU : out STD_LOGIC;
            TIE : out STD_LOGIC
    );
end blackjack;

architecture Behavioral of blackjack is
    type state_type is (
        STATE_INICIO,
        STATE_CARTA_USER_1, 
        STATE_CARTA_USER_2, 
        STATE_ESPERAR_USER,
        STATE_HIT,
        STATE_STAY,
        STATE_CARTA_1_DEALER, 
        STATE_CARTA_2_DEALER,
        STATE_ESPERAR_DEALER,
        STATE_NOVA_CARTA_DEALER, 
        STATE_COMPARAR_CARTAS,
        STATE_USER_GANHOU, 
        STATE_USER_PERDEU, 
        STATE_TIE
    );
    
    signal current_state, next_state : state_type;
    signal soma_user    : unsigned(7 downto 0) := (others => '0');
    signal soma_dealer  : unsigned(7 downto 0) := (others => '0');
    signal carta_atual  : unsigned(3 downto 0);
    signal ases_user    : unsigned(3 downto 0) := (others => '0');
    signal ases_dealer  : unsigned(3 downto 0) := (others => '0');
    
    function get_card_value(card: unsigned; current_sum: unsigned; num_aces: unsigned) return unsigned is
        variable card_value: unsigned(7 downto 0);
    begin
        if card = 1 then
            if current_sum <= 10 then
                card_value := to_unsigned(11, 8);
            else
                card_value := to_unsigned(1, 8);
            end if;
        elsif card >= 10 and card <= 13 then
            card_value := to_unsigned(10, 8);
        elsif card > 13 then
            card_value := to_unsigned(0, 8);
        else
            card_value := resize(card, 8);
        end if;
        return card_value;
    end function;
    
    function adjust_aces(sum: unsigned; num_aces: unsigned) return unsigned is
        variable adjusted_sum: unsigned(7 downto 0);
        variable needed_adjustments: integer;
    begin
        adjusted_sum := sum;
        
        needed_adjustments := to_integer(sum) / 10 - 2; 
    
        if needed_adjustments > 0 then
            adjusted_sum := adjusted_sum - to_unsigned(needed_adjustments * 10, adjusted_sum'length);
        end if;
        
        return adjusted_sum;
    end function;
    
    
begin
    -- Processo combinacional para atualizar displays
    process(current_state, carta_atual, soma_dealer, soma_user)
    begin
        -- Atualização imediata dos displays
        card_display <= std_logic_vector(carta_atual);
        if current_state = STATE_CARTA_1_DEALER or
           current_state = STATE_CARTA_2_DEALER or
           current_state = STATE_ESPERAR_DEALER or
           current_state = STATE_NOVA_CARTA_DEALER then
            sum_display <= std_logic_vector(soma_dealer);
        else
            sum_display <= std_logic_vector(soma_user);
        end if;
    end process;




    -- Processo de registrador de estado
    process(clk, rst)
    begin
        if rst = '1' then
            current_state <= STATE_INICIO;
            soma_user <= (others => '0');
            soma_dealer <= (others => '0');
            ases_user <= (others => '0');
            ases_dealer <= (others => '0');
        elsif rising_edge(clk) then
            current_state <= next_state;
            
            -- Atualização das somas e contagem de ases
            case current_state is
                when STATE_INICIO =>
                    soma_user <= (others => '0');
                    soma_dealer <= (others => '0');
                    ases_user <= (others => '0');
                    ases_dealer <= (others => '0');
                    
                when STATE_CARTA_USER_1 | STATE_CARTA_USER_2 | STATE_HIT =>
                    if carta_atual = 1 then
                        ases_user <= ases_user + 1;
                    end if;
                    soma_user <= adjust_aces(soma_user + get_card_value(carta_atual, soma_user, ases_user), ases_user);
                    
                when STATE_NOVA_CARTA_DEALER | STATE_CARTA_1_DEALER | STATE_CARTA_2_DEALER  =>
                    if carta_atual = 1 then
                        ases_dealer <= ases_dealer + 1;
                    end if;
                    soma_dealer <= adjust_aces(soma_dealer + get_card_value(carta_atual, soma_dealer, ases_dealer), ases_dealer);
                    
                when others =>
                    null;
            end case;
        end if;
    end process;
    
    process(current_state, start, hit_btn, stay_btn, random_cards, cards, soma_user, soma_dealer)
    begin
        -- Valores padrão
        next_state <= current_state;
        win_out <= '0';
        lose_out <= '0';
        tie_out <= '0';
        
        -- Atualização da carta atual baseada no estado
        if random_cards = '1' then
            case current_state is
                when STATE_CARTA_USER_1 => carta_atual <= "0001";
                when STATE_CARTA_USER_2 => carta_atual <= "0010";
                when STATE_HIT => carta_atual <= "0011";
                when STATE_CARTA_1_DEALER => carta_atual <= "0100";
                when STATE_CARTA_2_DEALER => carta_atual <= "0101";
                when STATE_NOVA_CARTA_DEALER => carta_atual <= "0110";
                when others => carta_atual <= "0000";
            end case;
        else
            carta_atual <= unsigned(cards);
        end if;
        
        case current_state is
            when STATE_INICIO =>
                if start = '1' then
                    next_state <= STATE_CARTA_USER_1;
                end if;
                
            when STATE_CARTA_USER_1 =>
                next_state <= STATE_CARTA_USER_2;
                
            when STATE_CARTA_USER_2 =>
                    next_state <= STATE_ESPERAR_USER;
                
            when STATE_ESPERAR_USER =>
                if hit_btn = '1' then
                    next_state <= STATE_HIT;
                elsif stay_btn = '1' then
                    next_state <= STATE_STAY;
                end if;
                if soma_user = 21 then
                    next_state <= STATE_USER_GANHOU;
                elsif soma_user > 21 then
                    next_state <= STATE_USER_PERDEU;
                end if;
                
            when STATE_HIT =>
                    next_state <= STATE_ESPERAR_USER;
                
            when STATE_STAY =>
                next_state <= STATE_CARTA_1_DEALER;
                
            when STATE_CARTA_1_DEALER =>
                next_state <= STATE_CARTA_2_DEALER;
                
            when STATE_CARTA_2_DEALER =>
                next_state <= STATE_ESPERAR_DEALER;

            when STATE_ESPERAR_DEALER =>
                if soma_dealer >= 17 then
                    next_state <= STATE_COMPARAR_CARTAS;
                else
                    next_state <= STATE_NOVA_CARTA_DEALER;
                end if;            

            when STATE_NOVA_CARTA_DEALER =>
                next_state <= STATE_ESPERAR_DEALER;

            when STATE_COMPARAR_CARTAS =>
                -- Condições atualizadas para comparação correta
                if soma_dealer > 21 then
                    -- Dealer estourou, usuário ganha
                    next_state <= STATE_USER_GANHOU;
                elsif soma_user = soma_dealer then
                    -- Empate
                    next_state <= STATE_TIE;
                elsif soma_user > soma_dealer then
                    -- Usuário tem pontuação maior
                    next_state <= STATE_USER_GANHOU;
                else
                    -- Dealer tem pontuação maior
                    next_state <= STATE_USER_PERDEU;
                end if;
                
            when STATE_USER_GANHOU =>
                win_out <= '1';
                if start = '1' then
                    next_state <= STATE_INICIO;
                end if;
                
            when STATE_USER_PERDEU =>
                lose_out <= '1';
                if start = '1' then
                    next_state <= STATE_INICIO;
                end if;
                
            when STATE_TIE =>
                tie_out <= '1';
                if start = '1' then
                    next_state <= STATE_INICIO;
                end if;
        end case;
    end process;






        -- Processo para localizar o estado atual
        process(current_state)
        begin
            -- Desativar todas as saídas inicialmente
            INICIO <= '0';
            CARTA_USER_1 <= '0';
            CARTA_USER_2 <= '0';
            ESPERAR_USER <= '0';
            HIT <= '0';
            STAY <= '0';
            CARTA_1_DEALER <= '0';
            CARTA_2_DEALER <= '0';
            NOVA_CARTA_DEALER <= '0';
            ESPERAR_DEALER <= '0';
            COMPARAR_CARTAS <= '0';
            USER_GANHOU <= '0';
            USER_PERDEU <= '0';
            TIE <= '0';
    
            case current_state is
                when STATE_INICIO =>
                    INICIO <= '1';
                when STATE_CARTA_USER_1 =>
                    CARTA_USER_1 <= '1';
                when STATE_CARTA_USER_2 =>
                    CARTA_USER_2 <= '1';
                when STATE_ESPERAR_USER =>
                    ESPERAR_USER <= '1';
                when STATE_HIT =>
                    HIT <= '1';
                when STATE_STAY =>
                    STAY <= '1';
                when STATE_CARTA_1_DEALER =>
                    CARTA_1_DEALER <= '1';
                when STATE_CARTA_2_DEALER =>
                    CARTA_2_DEALER <= '1';
                when STATE_NOVA_CARTA_DEALER =>
                    NOVA_CARTA_DEALER <= '1';
                when STATE_ESPERAR_DEALER =>
                    ESPERAR_DEALER <= '1';
                when STATE_COMPARAR_CARTAS =>
                    COMPARAR_CARTAS <= '1';
                when STATE_USER_GANHOU =>
                    USER_GANHOU <= '1';
                when STATE_USER_PERDEU =>
                    USER_PERDEU <= '1';
                when STATE_TIE =>
                    TIE <= '1';
                when others =>
                    null;
            end case;
        end process;
    
end Behavioral;
*/

/* Code of BCD_to_7Segment:
library IEEE;
use IEEE.STD_LOGIC_1164.ALL;

-- Entidade do decodificador
entity BCD_to_7Segment is
    Port (
        BCD : in STD_LOGIC_VECTOR(3 downto 0); -- Entrada BCD de 4 bits
        card_display: out STD_LOGIC_VECTOR(6 downto 0)  -- Saída do display de 7 segmentos
    );
end BCD_to_7Segment;

-- Arquitetura do decodificador
architecture Behavioral of BCD_to_7Segment is
begin
    -- Decodificação dos segmentos com base na entrada BCD
    process(BCD)
    begin
        case BCD is
            when "0001"  => card_display <= "1111001"; -- Representação do número 1
            when "0010"  => card_display <= "0100100"; -- Representação do número 2
            when "0011"  => card_display <= "0110000"; -- Representação do número 3
            when "0100"  => card_display <= "0011001"; -- Representação do número 4
            when "0101"  => card_display <= "0010010"; -- Representação do número 5
            when "0110"  => card_display <= "0000010"; -- Representação do número 6
            when "0111"  => card_display <= "1111000"; -- Representação do número 7
            when "1000"  => card_display <= "0000000"; -- Representação do número 8
            when "1001"  => card_display <= "0010000"; -- Representação do número 9
            when "1010"  => card_display <= "0001000"; -- Representação do número 10 (A)
            when "1011"  => card_display <= "0000011"; -- Representação do número 11 (B)
            when "1100"  => card_display <= "1000110"; -- Representação do número 12 (C)
            when "1101"  => card_display <= "0100001"; -- Representação do número 13 (D)
            when others  => card_display <= "0000000"; -- Valor padrão (caso de erro)
        end case;
    end process;
end Behavioral;
*/
