// Digital circuit implementacao.dig as structural Verilog
module implementacao (
  input  clk,
  input  rst,
  input  start,
  input  hit,
  input  stay,
  input  random,
  input  [3:0] cards
);

  wire u_BCD_to_7Segment_a, u_BCD_to_7Segment_b, u_BCD_to_7Segment_c, u_BCD_to_7Segment_d,
       u_BCD_to_7Segment_e, u_BCD_to_7Segment_f, u_BCD_to_7Segment_g, u_BCD_to_7Segment_p,
       u_blackjack_carta_1_dealer, u_blackjack_carta_2_dealer, u_blackjack_carta_user_1,
       u_blackjack_carta_user_2, u_blackjack_comparar_cartas, u_blackjack_esperar_user, u_blackjack_hit,
       u_blackjack_inicio, u_blackjack_lose_out, u_blackjack_nova_carta_dealer, u_blackjack_stay,
       u_blackjack_tie, u_blackjack_tie_out, u_blackjack_user_ganhou, u_blackjack_user_perdeu,
       u_blackjack_win_out, u_Display_Controller_2_a1, u_Display_Controller_2_a2, u_Display_Controller_2_b1,
       u_Display_Controller_2_b2, u_Display_Controller_2_c1, u_Display_Controller_2_c2,
       u_Display_Controller_2_d1, u_Display_Controller_2_d2, u_Display_Controller_2_e1,
       u_Display_Controller_2_e2, u_Display_Controller_2_f1, u_Display_Controller_2_f2,
       u_Display_Controller_2_g1, u_Display_Controller_2_g2, u_Display_Controller_2_p1,
       u_Display_Controller_2_p2, u_Display_Controller_3_a1, u_Display_Controller_3_a2,
       u_Display_Controller_3_b1, u_Display_Controller_3_b2, u_Display_Controller_3_c1,
       u_Display_Controller_3_c2, u_Display_Controller_3_d1, u_Display_Controller_3_d2,
       u_Display_Controller_3_e1, u_Display_Controller_3_e2, u_Display_Controller_3_f1,
       u_Display_Controller_3_f2, u_Display_Controller_3_g1, u_Display_Controller_3_g2,
       u_Display_Controller_3_p1, u_Display_Controller_3_p2, u_Display_Controller_a1,
       u_Display_Controller_a2, u_Display_Controller_b1, u_Display_Controller_b2, u_Display_Controller_c1,
       u_Display_Controller_c2, u_Display_Controller_d1, u_Display_Controller_d2, u_Display_Controller_e1,
       u_Display_Controller_e2, u_Display_Controller_f1, u_Display_Controller_f2, u_Display_Controller_g1,
       u_Display_Controller_g2, u_Display_Controller_p1, u_Display_Controller_p2;
  wire [3:0] u_blackjack_card_display;
  wire [7:0] u_blackjack_soma_dealer_display, u_blackjack_soma_user_display, u_blackjack_sum_display;

  Display_Controller #(.applicationType("GHDL")) u_Display_Controller (
    .sum_display(u_blackjack_sum_display), .a1(u_Display_Controller_a1), .b1(u_Display_Controller_b1),
    .c1(u_Display_Controller_c1), .d1(u_Display_Controller_d1), .e1(u_Display_Controller_e1),
    .f1(u_Display_Controller_f1), .g1(u_Display_Controller_g1), .p1(u_Display_Controller_p1),
    .a2(u_Display_Controller_a2), .b2(u_Display_Controller_b2), .c2(u_Display_Controller_c2),
    .d2(u_Display_Controller_d2), .e2(u_Display_Controller_e2), .f2(u_Display_Controller_f2),
    .g2(u_Display_Controller_g2), .p2(u_Display_Controller_p2));
  blackjack #(.applicationType("GHDL")) u_blackjack (
    .clk(clk), .rst(rst), .start(start), .hit_btn(hit), .stay_btn(stay), .random_cards(random),
    .cards(cards), .win_out(u_blackjack_win_out), .lose_out(u_blackjack_lose_out),
    .tie_out(u_blackjack_tie_out), .card_display(u_blackjack_card_display),
    .sum_display(u_blackjack_sum_display), .soma_user_display(u_blackjack_soma_user_display),
    .soma_dealer_display(u_blackjack_soma_dealer_display), .INICIO(u_blackjack_inicio),
    .CARTA_USER_1(u_blackjack_carta_user_1), .CARTA_USER_2(u_blackjack_carta_user_2),
    .ESPERAR_USER(u_blackjack_esperar_user), .HIT(u_blackjack_hit), .STAY(u_blackjack_stay),
    .CARTA_1_DEALER(u_blackjack_carta_1_dealer), .CARTA_2_DEALER(u_blackjack_carta_2_dealer),
    .NOVA_CARTA_DEALER(u_blackjack_nova_carta_dealer), .COMPARAR_CARTAS(u_blackjack_comparar_cartas),
    .USER_GANHOU(u_blackjack_user_ganhou), .USER_PERDEU(u_blackjack_user_perdeu), .TIE(u_blackjack_tie));
  Seven_Seg seven_seg_1 (
    .a(u_Display_Controller_a2), .b(u_Display_Controller_b2), .c(u_Display_Controller_c2),
    .d(u_Display_Controller_d2), .e(u_Display_Controller_e2), .f(u_Display_Controller_f2),
    .g(u_Display_Controller_g2), .dp(u_Display_Controller_p2));
  Seven_Seg seven_seg_2 (
    .a(u_Display_Controller_a1), .b(u_Display_Controller_b1), .c(u_Display_Controller_c1),
    .d(u_Display_Controller_d1), .e(u_Display_Controller_e1), .f(u_Display_Controller_f1),
    .g(u_Display_Controller_g1), .dp(u_Display_Controller_p1));
  BCD_to_7Segment #(.applicationType("GHDL")) u_BCD_to_7Segment (
    .BCD(u_blackjack_card_display), .a(u_BCD_to_7Segment_a), .b(u_BCD_to_7Segment_b),
    .c(u_BCD_to_7Segment_c), .d(u_BCD_to_7Segment_d), .e(u_BCD_to_7Segment_e), .f(u_BCD_to_7Segment_f),
    .g(u_BCD_to_7Segment_g), .p(u_BCD_to_7Segment_p));
  LED WIN_OUT (.in(u_blackjack_win_out));
  LED LOSE_OUT (.in(u_blackjack_lose_out));
  LED TIE_OUT (.in(u_blackjack_tie_out));
  Seven_Seg seven_seg_3 (
    .a(u_BCD_to_7Segment_a), .b(u_BCD_to_7Segment_b), .c(u_BCD_to_7Segment_c), .d(u_BCD_to_7Segment_d),
    .e(u_BCD_to_7Segment_e), .f(u_BCD_to_7Segment_f), .g(u_BCD_to_7Segment_g), .dp(u_BCD_to_7Segment_p));
  Display_Controller #(.applicationType("GHDL")) u_Display_Controller_2 (
    .sum_display(u_blackjack_soma_user_display), .a1(u_Display_Controller_2_a1),
    .b1(u_Display_Controller_2_b1), .c1(u_Display_Controller_2_c1), .d1(u_Display_Controller_2_d1),
    .e1(u_Display_Controller_2_e1), .f1(u_Display_Controller_2_f1), .g1(u_Display_Controller_2_g1),
    .p1(u_Display_Controller_2_p1), .a2(u_Display_Controller_2_a2), .b2(u_Display_Controller_2_b2),
    .c2(u_Display_Controller_2_c2), .d2(u_Display_Controller_2_d2), .e2(u_Display_Controller_2_e2),
    .f2(u_Display_Controller_2_f2), .g2(u_Display_Controller_2_g2), .p2(u_Display_Controller_2_p2));
  LED INICIO (.in(u_blackjack_inicio));
  LED CARTA_USER_1 (.in(u_blackjack_carta_user_1));
  LED CARTA_USER_2 (.in(u_blackjack_carta_user_2));
  LED ESPERAR_USER (.in(u_blackjack_esperar_user));
  LED u_HIT (.in(u_blackjack_hit));
  LED u_STAY (.in(u_blackjack_stay));
  LED CARTA_1_DEALER (.in(u_blackjack_carta_1_dealer));
  LED CARTA_2_DEALER (.in(u_blackjack_carta_2_dealer));
  LED NOVA_CARTA_DEALER (.in(u_blackjack_nova_carta_dealer));
  LED COMPARAR_CARTAS (.in(u_blackjack_comparar_cartas));
  LED USER_GANHOU (.in(u_blackjack_user_ganhou));
  LED USER_PERDEU (.in(u_blackjack_user_perdeu));
  LED TIE (.in(u_blackjack_tie));
  Display_Controller #(.applicationType("GHDL")) u_Display_Controller_3 (
    .sum_display(u_blackjack_soma_dealer_display), .a1(u_Display_Controller_3_a1),
    .b1(u_Display_Controller_3_b1), .c1(u_Display_Controller_3_c1), .d1(u_Display_Controller_3_d1),
    .e1(u_Display_Controller_3_e1), .f1(u_Display_Controller_3_f1), .g1(u_Display_Controller_3_g1),
    .p1(u_Display_Controller_3_p1), .a2(u_Display_Controller_3_a2), .b2(u_Display_Controller_3_b2),
    .c2(u_Display_Controller_3_c2), .d2(u_Display_Controller_3_d2), .e2(u_Display_Controller_3_e2),
    .f2(u_Display_Controller_3_f2), .g2(u_Display_Controller_3_g2), .p2(u_Display_Controller_3_p2));
  Seven_Seg seven_seg_4 (
    .a(u_Display_Controller_2_a2), .b(u_Display_Controller_2_b2), .c(u_Display_Controller_2_c2),
    .d(u_Display_Controller_2_d2), .e(u_Display_Controller_2_e2), .f(u_Display_Controller_2_f2),
    .g(u_Display_Controller_2_g2), .dp(u_Display_Controller_2_p2));
  Seven_Seg seven_seg_5 (
    .a(u_Display_Controller_2_a1), .b(u_Display_Controller_2_b1), .c(u_Display_Controller_2_c1),
    .d(u_Display_Controller_2_d1), .e(u_Display_Controller_2_e1), .f(u_Display_Controller_2_f1),
    .g(u_Display_Controller_2_g1), .dp(u_Display_Controller_2_p1));
  Seven_Seg seven_seg_6 (
    .a(u_Display_Controller_3_a2), .b(u_Display_Controller_3_b2), .c(u_Display_Controller_3_c2),
    .d(u_Display_Controller_3_d2), .e(u_Display_Controller_3_e2), .f(u_Display_Controller_3_f2),
    .g(u_Display_Controller_3_g2), .dp(u_Display_Controller_3_p2));
  Seven_Seg seven_seg_7 (
    .a(u_Display_Controller_3_a1), .b(u_Display_Controller_3_b1), .c(u_Display_Controller_3_c1),
    .d(u_Display_Controller_3_d1), .e(u_Display_Controller_3_e1), .f(u_Display_Controller_3_f1),
    .g(u_Display_Controller_3_g1), .dp(u_Display_Controller_3_p1));
endmodule

/* Code of Display_Controller:
library IEEE;
use IEEE.STD_LOGIC_1164.ALL;
use IEEE.NUMERIC_STD.ALL;

entity Display_Controller is
    Port (
        sum_display : in STD_LOGIC_VECTOR(7 downto 0);
        -- Saídas para o primeiro display (unidades)
        a1, b1, c1, d1, e1, f1, g1, p1 : out STD_LOGIC;
        -- Saídas para o segundo display (dezenas)
        a2, b2, c2, d2, e2, f2, g2, p2 : out STD_LOGIC
    );
end Display_Controller;

architecture Behavioral of Display_Controller is
    -- Sinais intermediários para armazenar valores decimais
    signal binary_value : integer range 0 to 255;
    signal tens, ones : integer range 0 to 9;
    signal tens_bcd, ones_bcd : STD_LOGIC_VECTOR(3 downto 0);

begin
    -- Converte o valor binário para inteiro
    binary_value <= to_integer(unsigned(sum_display));
    
    -- Calcula dezenas e unidades
    tens <= binary_value / 10;
    ones <= binary_value mod 10;
    
    -- Converte os valores para BCD
    tens_bcd <= std_logic_vector(to_unsigned(tens, 4));
    ones_bcd <= std_logic_vector(to_unsigned(ones, 4));
    
    -- Processo para decodificar o dígito das unidades
    process(ones_bcd)
    begin
        case ones_bcd is
            when "0000" => -- 0
                a1 <= '1'; b1 <= '1'; c1 <= '1'; d1 <= '1'; e1 <= '1'; f1 <= '1'; g1 <= '0';
            when "0001" => -- 1
                a1 <= '0'; b1 <= '1'; c1 <= '1'; d1 <= '0'; e1 <= '0'; f1 <= '0'; g1 <= '0';
            when "0010" => -- 2
                a1 <= '1'; b1 <= '1'; c1 <= '0'; d1 <= '1'; e1 <= '1'; f1 <= '0'; g1 <= '1';
            when "0011" => -- 3
                a1 <= '1'; b1 <= '1'; c1 <= '1'; d1 <= '1'; e1 <= '0'; f1 <= '0'; g1 <= '1';
            when "0100" => -- 4
                a1 <= '0'; b1 <= '1'; c1 <= '1'; d1 <= '0'; e1 <= '0'; f1 <= '1'; g1 <= '1';
            when "0101" => -- 5
                a1 <= '1'; b1 <= '0'; c1 <= '1'; d1 <= '1'; e1 <= '0'; f1 <= '1'; g1 <= '1';
            when "0110" => -- 6
                a1 <= '1'; b1 <= '0'; c1 <= '1'; d1 <= '1'; e1 <= '1'; f1 <= '1'; g1 <= '1';
            when "0111" => -- 7
                a1 <= '1'; b1 <= '1'; c1 <= '1'; d1 <= '0'; e1 <= '0'; f1 <= '0'; g1 <= '0';
            when "1000" => -- 8
                a1 <= '1'; b1 <= '1'; c1 <= '1'; d1 <= '1'; e1 <= '1'; f1 <= '1'; g1 <= '1';
            when "1001" => -- 9
                a1 <= '1'; b1 <= '1'; c1 <= '1'; d1 <= '1'; e1 <= '0'; f1 <= '1'; g1 <= '1';
            when others => -- Desativa todos os segmentos
                a1 <= '0'; b1 <= '0'; c1 <= '0'; d1 <= '0'; e1 <= '0'; f1 <= '0'; g1 <= '0';
        end case;
    end process;
    
    -- Processo para decodificar o dígito das dezenas
    process(tens_bcd)
    begin
        case tens_bcd is
            when "0000" => -- 0
                a2 <= '1'; b2 <= '1'; c2 <= '1'; d2 <= '1'; e2 <= '1'; f2 <= '1'; g2 <= '0';
            when "0001" => -- 1
                a2 <= '0'; b2 <= '1'; c2 <= '1'; d2 <= '0'; e2 <= '0'; f2 <= '0'; g2 <= '0';
            when "0010" => -- 2
                a2 <= '1'; b2 <= '1'; c2 <= '0'; d2 <= '1'; e2 <= '1'; f2 <= '0'; g2 <= '1';
            when "0011" => -- 3
                a2 <= '1'; b2 <= '1'; c2 <= '1'; d2 <= '1'; e2 <= '0'; f2 <= '0'; g2 <= '1';
            when "0100" => -- 4
                a2 <= '0'; b2 <= '1'; c2 <= '1'; d2 <= '0'; e2 <= '0'; f2 <= '1'; g2 <= '1';
            when "0101" => -- 5
                a2 <= '1'; b2 <= '0'; c2 <= '1'; d2 <= '1'; e2 <= '0'; f2 <= '1'; g2 <= '1';
            when "0110" => -- 6
                a2 <= '1'; b2 <= '0'; c2 <= '1'; d2 <= '1'; e2 <= '1'; f2 <= '1'; g2 <= '1';
            when "0111" => -- 7
                a2 <= '1'; b2 <= '1'; c2 <= '1'; d2 <= '0'; e2 <= '0'; f2 <= '0'; g2 <= '0';
            when "1000" => -- 8
                a2 <= '1'; b2 <= '1'; c2 <= '1'; d2 <= '1'; e2 <= '1'; f2 <= '1'; g2 <= '1';
            when "1001" => -- 9
                a2 <= '1'; b2 <= '1'; c2 <= '1'; d2 <= '1'; e2 <= '0'; f2 <= '1'; g2 <= '1';
            when others => -- Desativa todos os segmentos
                a2 <= '0'; b2 <= '0'; c2 <= '0'; d2 <= '0'; e2 <= '0'; f2 <= '0'; g2 <= '0';
        end case;
    end process;
    
end Behavioral;
*/

/* Code of blackjack:
library IEEE;
use IEEE.STD_LOGIC_1164.ALL;
use IEEE.NUMERIC_STD.ALL;

entity blackjack is
    Port ( 
        clk         : in  STD_LOGIC;
        rst         : in  STD_LOGIC;
        start       : in  STD_LOGIC;
        hit_btn     : in  STD_LOGIC;
        stay_btn    : in  STD_LOGIC;
        random_cards: in  STD_LOGIC;  
        cards       : in  STD_LOGIC_VECTOR(3 downto 0);
        
        win_out     : out STD_LOGIC;
        lose_out    : out STD_LOGIC;
        tie_out     : out STD_LOGIC;
        card_display: out STD_LOGIC_VECTOR(3 downto 0);
        sum_display : out STD_LOGIC_VECTOR(7 downto 0);

        soma_user_display   : out STD_LOGIC_VECTOR(7 downto 0);
        soma_dealer_display : out STD_LOGIC_VECTOR(7 downto 0);

        INICIO : out STD_LOGIC;
        CARTA_USER_1 : out STD_LOGIC;
        CARTA_USER_2 : out STD_LOGIC;
        ESPERAR_USER: out STD_LOGIC;
        HIT : out STD_LOGIC;
        STAY : out STD_LOGIC;
        CARTA_1_DEALER : out STD_LOGIC;
        CARTA_2_DEALER : out STD_LOGIC;
        NOVA_CARTA_DEALER : out STD_LOGIC;
        COMPARAR_CARTAS : out STD_LOGIC;
        USER_GANHOU : out STD_LOGIC;
        USER_PERDEU : out STD_LOGIC;
        TIE : out STD_LOGIC
    );
end blackjack;

architecture Behavioral of blackjack is
    type state_type is (
        STATE_INICIO,
        STATE_CARTA_USER_1, 
        STATE_CARTA_USER_2, 
        STATE_ESPERAR_USER,
        STATE_HIT,
        STATE_STAY,
        STATE_CARTA_1_DEALER, 
        STATE_CARTA_2_DEALER,
        STATE_NOVA_CARTA_DEALER, 
        STATE_COMPARAR_CARTAS,
        STATE_USER_GANHOU, 
        STATE_USER_PERDEU, 
        STATE_TIE
    );
    
    signal current_state, next_state : state_type;
    signal soma_user    : unsigned(7 downto 0) := (others => '0');
    signal soma_dealer  : unsigned(7 downto 0) := (others => '0');
    signal carta_atual  : unsigned(3 downto 0);
    signal ases_user    : unsigned(3 downto 0) := (others => '0');
    signal ases_dealer  : unsigned(3 downto 0) := (others => '0');
    
    function get_card_value(card: unsigned; current_sum: unsigned; num_aces: unsigned) return unsigned is
        variable card_value: unsigned(7 downto 0);
    begin
        if card = 1 then
            if current_sum <= 10 then
                card_value := to_unsigned(11, 8);
            else
                card_value := to_unsigned(1, 8);
            end if;
        elsif card >= 10 and card <= 13 then
            card_value := to_unsigned(10, 8);
        elsif card > 13 then
            card_value := to_unsigned(0, 8);
        else
            card_value := resize(card, 8);
        end if;
        return card_value;
    end function;
    
    function adjust_aces(sum: unsigned; num_aces: unsigned) return unsigned is
        variable adjusted_sum: unsigned(7 downto 0);
    begin
        adjusted_sum := sum;
        for i in 0 to to_integer(num_aces)-1 loop
            if adjusted_sum > 21 then
                adjusted_sum := adjusted_sum - 10;
            end if;
        end loop;
        return adjusted_sum;
    end function;
    
begin
    -- Processo combinacional para atualizar displays
    process(current_state, carta_atual, soma_dealer, soma_user)
    begin
        -- Atualização imediata dos displays
        card_display <= std_logic_vector(carta_atual);
        if current_state = STATE_CARTA_1_DEALER or 
           current_state = STATE_CARTA_2_DEALER or 
           current_state = STATE_NOVA_CARTA_DEALER then
            sum_display <= std_logic_vector(soma_dealer);
        else
            sum_display <= std_logic_vector(soma_user);
        end if;
    end process;

    -- Debug displays soma dos jogadores
    process(current_state)
    begin
        soma_user_display   <= std_logic_vector(soma_user);
        soma_dealer_display <= std_logic_vector(soma_dealer);
    end process;

    -- Processo de registrador de estado
    process(clk, rst)
    begin
        if rst = '1' then
            current_state <= STATE_INICIO;
            soma_user <= (others => '0');
            soma_dealer <= (others => '0');
            ases_user <= (others => '0');
            ases_dealer <= (others => '0');
        elsif rising_edge(clk) then
            current_state <= next_state;
            
            -- Atualização das somas e contagem de ases
            case current_state is
                when STATE_INICIO =>
                    soma_user <= (others => '0');
                    soma_dealer <= (others => '0');
                    ases_user <= (others => '0');
                    ases_dealer <= (others => '0');
                    
                when STATE_CARTA_USER_1 | STATE_CARTA_USER_2 | STATE_HIT =>
                    if carta_atual = 1 then
                        ases_user <= ases_user + 1;
                    end if;
                    soma_user <= adjust_aces(soma_user + get_card_value(carta_atual, soma_user, ases_user), ases_user);
                    
                when STATE_CARTA_1_DEALER | STATE_CARTA_2_DEALER | STATE_NOVA_CARTA_DEALER =>
                    if carta_atual = 1 then
                        ases_dealer <= ases_dealer + 1;
                    end if;
                    soma_dealer <= adjust_aces(soma_dealer + get_card_value(carta_atual, soma_dealer, ases_dealer), ases_dealer);
                    
                when others =>
                    null;
            end case;
        end if;
    end process;
    
    process(current_state, start, hit_btn, stay_btn, random_cards, cards, soma_user, soma_dealer)
    begin
        -- Valores padrão
        next_state <= current_state;
        win_out <= '0';
        lose_out <= '0';
        tie_out <= '0';
        
        -- Atualização da carta atual baseada no estado
        if random_cards = '1' then
            case current_state is
                when STATE_CARTA_USER_1 => carta_atual <= "0001";
                when STATE_CARTA_USER_2 => carta_atual <= "0010";
                when STATE_HIT => carta_atual <= "0011";
                when STATE_CARTA_1_DEALER => carta_atual <= "0100";
                when STATE_CARTA_2_DEALER => carta_atual <= "0101";
                when STATE_NOVA_CARTA_DEALER => carta_atual <= "0110";
                when others => carta_atual <= "0000";
            end case;
        else
            carta_atual <= unsigned(cards);
        end if;
        
        case current_state is
            when STATE_INICIO =>
                if start = '1' then
                    next_state <= STATE_CARTA_USER_1;
                end if;
                
            when STATE_CARTA_USER_1 =>
                next_state <= STATE_CARTA_USER_2;
                
            when STATE_CARTA_USER_2 =>
                    next_state <= STATE_ESPERAR_USER;
                
            when STATE_ESPERAR_USER =>
                if hit_btn = '1' then
                    next_state <= STATE_HIT;
                elsif stay_btn = '1' then
                    next_state <= STATE_STAY;
                end if;
                if soma_user = 21 then
                    next_state <= STATE_USER_GANHOU;
                elsif soma_user > 21 then
                    next_state <= STATE_USER_PERDEU;
                end if;
                
            when STATE_HIT =>
                    next_state <= STATE_ESPERAR_USER;
                
            when STATE_STAY =>
                next_state <= STATE_CARTA_1_DEALER;
                
            when STATE_CARTA_1_DEALER =>
                next_state <= STATE_CARTA_2_DEALER;
                
            when STATE_CARTA_2_DEALER =>
                if soma_dealer >= 17 then
                    next_state <= STATE_COMPARAR_CARTAS;
                else
                    next_state <= STATE_NOVA_CARTA_DEALER;
                end if;
                
            when STATE_NOVA_CARTA_DEALER =>
                if soma_dealer >= 17 then
                    next_state <= STATE_COMPARAR_CARTAS;
                else
                    -- Se a soma ainda não atingiu 17, continua sacando cartas
                    next_state <= STATE_NOVA_CARTA_DEALER;
                end if;
                
            when STATE_COMPARAR_CARTAS =>
                if soma_dealer > 21 then
                    next_state <= STATE_USER_GANHOU;
                elsif soma_user = soma_dealer then
                    next_state <= STATE_TIE;
                elsif soma_user > soma_dealer then
                    next_state <= STATE_USER_GANHOU;
                else
                    next_state <= STATE_USER_PERDEU;
                end if;
                
            when STATE_USER_GANHOU =>
                win_out <= '1';
                if start = '1' then
                    next_state <= STATE_INICIO;
                end if;
                
            when STATE_USER_PERDEU =>
                lose_out <= '1';
                if start = '1' then
                    next_state <= STATE_INICIO;
                end if;
                
            when STATE_TIE =>
                tie_out <= '1';
                if start = '1' then
                    next_state <= STATE_INICIO;
                end if;
        end case;
    end process;

    -- Processo para localizar o estado atual
    process(current_state)
    begin
        -- Desativar todas as saídas inicialmente
        INICIO <= '0';
        CARTA_USER_1 <= '0';
        CARTA_USER_2 <= '0';
        ESPERAR_USER <= '0';
        HIT <= '0';
        STAY <= '0';
        CARTA_1_DEALER <= '0';
        CARTA_2_DEALER <= '0';
        NOVA_CARTA_DEALER <= '0';
        COMPARAR_CARTAS <= '0';
        USER_GANHOU <= '0';
        USER_PERDEU <= '0';
        TIE <= '0';

        case current_state is
            when STATE_INICIO =>
                INICIO <= '1';
            when STATE_CARTA_USER_1 =>
                CARTA_USER_1 <= '1';
            when STATE_CARTA_USER_2 =>
                CARTA_USER_2 <= '1';
            when STATE_ESPERAR_USER =>
                ESPERAR_USER <= '1';
            when STATE_HIT =>
                HIT <= '1';
            when STATE_STAY =>
                STAY <= '1';
            when STATE_CARTA_1_DEALER =>
                CARTA_1_DEALER <= '1';
            when STATE_CARTA_2_DEALER =>
                CARTA_2_DEALER <= '1';
            when STATE_NOVA_CARTA_DEALER =>
                NOVA_CARTA_DEALER <= '1';
            when STATE_COMPARAR_CARTAS =>
                COMPARAR_CARTAS <= '1';
            when STATE_USER_GANHOU =>
                USER_GANHOU <= '1';
            when STATE_USER_PERDEU =>
                USER_PERDEU <= '1';
            when STATE_TIE =>
                TIE <= '1';
            when others =>
                null;
        end case;
    end process;

end Behavioral;
*/

/* Code of BCD_to_7Segment:
library IEEE;
use IEEE.STD_LOGIC_1164.ALL;

-- Entidade do decodificador
entity BCD_to_7Segment is
    Port (
        BCD : in STD_LOGIC_VECTOR(3 downto 0); -- Entrada BCD de 4 bits
        a, b, c, d, e, f, g, p : out STD_LOGIC -- Saídas individuais para cada segmento
    );
end BCD_to_7Segment;

-- Arquitetura do decodificador
architecture Behavioral of BCD_to_7Segment is
begin
    -- Decodificação dos segmentos com base na entrada BCD
    process(BCD)
    begin
        case BCD is
            when "0000" => -- 0
                a <= '1'; b <= '1'; c <= '1'; d <= '1'; e <= '1'; f <= '1'; g <= '0';
            when "0001" => -- 1
                a <= '0'; b <= '1'; c <= '1'; d <= '0'; e <= '0'; f <= '0'; g <= '0';
            when "0010" => -- 2
                a <= '1'; b <= '1'; c <= '0'; d <= '1'; e <= '1'; f <= '0'; g <= '1';
            when "0011" => -- 3
                a <= '1'; b <= '1'; c <= '1'; d <= '1'; e <= '0'; f <= '0'; g <= '1';
            when "0100" => -- 4
                a <= '0'; b <= '1'; c <= '1'; d <= '0'; e <= '0'; f <= '1'; g <= '1';
            when "0101" => -- 5
                a <= '1'; b <= '0'; c <= '1'; d <= '1'; e <= '0'; f <= '1'; g <= '1';
            when "0110" => -- 6
                a <= '1'; b <= '0'; c <= '1'; d <= '1'; e <= '1'; f <= '1'; g <= '1';
            when "0111" => -- 7
                a <= '1'; b <= '1'; c <= '1'; d <= '0'; e <= '0'; f <= '0'; g <= '0';
            when "1000" => -- 8
                a <= '1'; b <= '1'; c <= '1'; d <= '1'; e <= '1'; f <= '1'; g <= '1';
            when "1001" => -- 9
                a <= '1'; b <= '1'; c <= '1'; d <= '1'; e <= '0'; f <= '1'; g <= '1';
            when "1010" => -- 10 (A)
                a <= '1'; b <= '1'; c <= '1'; d <= '0'; e <= '1'; f <= '1'; g <= '1';
            when "1011" => -- 11 (b)
                a <= '0'; b <= '0'; c <= '1'; d <= '1'; e <= '1'; f <= '1'; g <= '1';
            when "1100" => -- 12 (C)
                a <= '1'; b <= '0'; c <= '0'; d <= '1'; e <= '1'; f <= '1'; g <= '0';
            when "1101" => -- 13 (d)
                a <= '0'; b <= '1'; c <= '1'; d <= '1'; e <= '1'; f <= '0'; g <= '1';
            when others => -- Desativa todos os segmentos
                a <= '0'; b <= '0'; c <= '0'; d <= '0'; e <= '0'; f <= '0'; g <= '0';
        end case;
    end process;
end Behavioral;
*/
